// Logisim project 8bitcomputer.circ as structural Verilog: 16 circuits, main circuit main
// RO
module main (
  input  in_1,
  input  [7:0] in_2,
  input  [7:0] in_3,
  input  [3:0] in_4,
  input  in_5,
  input  in_6,
  input  in_7
);

  wire AI, AO, BI, button_1_out, button_2_out, CE, CF, CLK, clock_1_out, CO, EO, FI, HLT, II, IO, Jump, MI,
       not_1_out, OI, RI, RO, RST, STEP_RST, SUB, T5, ZF;
  wire [3:0] programcounter_1_output, ram_built_in_1_out_13;
  wire [7:0] ALUOUT, AOUT, B, b2d_1_out_5, b2d_1_out_6, b2d_1_out_7, BOUT;

  Button button_1 (.out(button_1_out));
  LED led_1 (.in(B[7]));
  LED led_2 (.in(B[4]));
  LED led_3 (.in(B[5]));
  LED led_4 (.in(B[6]));
  LED led_5 (.in(B[3]));
  assign B = in_1 ? in_2 : 8'bz;  // Controlled_Buffer controlled_buffer_1
  IR ir_1 (.in_1(II), .in_2(IO), .in_3(B), .in_4(CLK), .in_5(RST), .out_6(B));
  control_logic control_logic_1 (
    .in_1(CLK), .II(II), .out_7(HLT), .out_8(MI), .out_9(RI), .out_10(RO), .out_11(IO), .out_12(II),
    .out_13(AI), .T5(T5), .out_15(AO), .out_16(EO), .out_17(SUB), .out_18(BI), .out_19(OI), .out_20(CE),
    .out_21(CO), .out_22(Jump), .STEP_RST(STEP_RST), .RST(RST), .INSTRUCTION(B[7:4]), .out_23(FI),
    .Carry({ZF, CF}));
  LED led_6 (.in(B[0]));
  LED led_7 (.in(B[2]));
  LED led_8 (.in(B[1]));
  DotMatrix #(.matrixcols(8), .matrixrows(1), .dotshape("circle")) dotmatrix_1 (
    .col0(B[7]), .col1(B[6]), .col2(B[5]), .col3(B[4]), .col4(B[3]), .col5(B[2]), .col6(B[1]), .col7(B[0]));
  DotMatrix #(.matrixcols(4), .matrixrows(1), .dotshape("circle")) dotmatrix_2 (
    .col0(ram_built_in_1_out_13[3]), .col1(ram_built_in_1_out_13[2]), .col2(ram_built_in_1_out_13[1]),
    .col3(ram_built_in_1_out_13[0]));
  RAM_BUILT_IN ram_built_in_1 (
    .in_1(B), .in_2(in_3), .M_In(in_4), .in_5(RST), .SEL(in_6), .in_8(in_5), .in_10(CLK), .in_6(RO),
    .in_9(RI), .in_11(MI), .out_14(B), .out_13(ram_built_in_1_out_13), .in_7(in_7), .in_12(button_1_out));
  alu_main alu_main_1 (
    .SUB(SUB), .EN(EO), .in_3(BOUT), .in_4(AOUT), .Result(B), .Result_2(ALUOUT), .out_9(ZF), .out_8(CF),
    .in_7(CLK), .in_5(FI), .in_6(RST));
  Clock clock_1 (.out(clock_1_out));
  assign CLK = not_1_out ? clock_1_out : 1'bz;  // Controlled_Buffer controlled_buffer_2
  not not_1 (not_1_out, HLT);
  Button button_2 (.out(button_2_out));
  Hex_Digit_Display hex_digit_display_1 (.value(b2d_1_out_7[3:0]));  // open: dp
  Hex_Digit_Display hex_digit_display_2 (.value(b2d_1_out_6[3:0]));  // open: dp
  b2d b2d_1 (
    .in_2(B), .out_5(b2d_1_out_5), .out_6(b2d_1_out_6), .out_7(b2d_1_out_7), .in_1(OI), .in_3(CLK), .in_4(RST));
  A_REG a_reg_1 (.in_1(AI), .in_2(1'b1), .in_3(B), .in_4(CLK), .in_5(RST), .out_6(AOUT));
  B_REG b_reg_1 (.in_1(BI), .in_2(1'b1), .in_3(B), .in_4(CLK), .in_5(RST), .out_6(BOUT));
  reset reset_1 (.in_1(button_2_out), .in_2(T5), .out_4(RST), .out_5(STEP_RST));  // open: out_3
  Hex_Digit_Display hex_digit_display_3 (.value(b2d_1_out_5[3:0]));  // open: dp
  assign B = AO ? AOUT : 8'bz;  // Controlled_Buffer controlled_buffer_3
  DotMatrix #(.matrixcols(8), .matrixrows(1), .dotshape("circle")) dotmatrix_3 (
    .col0(AOUT[7]), .col1(AOUT[6]), .col2(AOUT[5]), .col3(AOUT[4]), .col4(AOUT[3]), .col5(AOUT[2]),
    .col6(AOUT[1]), .col7(AOUT[0]));
  DotMatrix #(.matrixcols(8), .matrixrows(1), .dotshape("circle")) dotmatrix_4 (
    .col0(BOUT[7]), .col1(BOUT[6]), .col2(BOUT[5]), .col3(BOUT[4]), .col4(BOUT[3]), .col5(BOUT[2]),
    .col6(BOUT[1]), .col7(BOUT[0]));
  DotMatrix #(.matrixcols(8), .matrixrows(1), .dotshape("circle")) dotmatrix_5 (
    .col0(ALUOUT[7]), .col1(ALUOUT[6]), .col2(ALUOUT[5]), .col3(ALUOUT[4]), .col4(ALUOUT[3]),
    .col5(ALUOUT[2]), .col6(ALUOUT[1]), .col7(ALUOUT[0]));
  assign B[3:0] = CO ? programcounter_1_output : 4'bz;  // Controlled_Buffer Output_enable
  programcounter programcounter_1 (
    .Jump(Jump), .\input (B[3:0]), .Count_Enable(CE), .Clock(CLK), .Clear(RST),
    .Output(programcounter_1_output));

  // Other names for the same wires on the sheet: B1[3:0] = B[3:0]; Pc[7:0] = B; Pc2[7:0] = B; B2[3:0] = B[7:4];
  //   Instruc[3:0] = B[7:4]

  // Notes on the sheet:
  //   BUS
  //   RAM
  //   IR
  //   CONTROL
  //   LOGIC
  //   WR
  //   FIRST 4 
  //   NEXT 4
  //   OUTPUT
  //   CLOCK
  //   CONTROL SIGNALS
  //   REGISTER A
  //   ALU
  //   REGISTER B
  //   WR
  //   WR
  //   EN
  //   EN
  //   PROGRAM
  //   COUNTER
endmodule

module full__adder (
  input  A,
  input  B,
  input  Cin,
  output S,
  output Co
);

  wire and_1_out, and_2_out, and_3_out, and_4_out, and_5_out, and_6_out, not_1_out, not_2_out, not_3_out,
       not_4_out, or_1_out;

  not not_1 (not_1_out, B);
  not not_2 (not_2_out, A);
  and and_1 (and_1_out, not_1_out, A);
  and and_2 (and_2_out, B, not_2_out);
  or or_1 (or_1_out, and_1_out, and_2_out);
  and and_3 (and_3_out, A, B);
  not not_3 (not_3_out, Cin);
  not not_4 (not_4_out, or_1_out);
  and and_4 (and_4_out, Cin, or_1_out);
  and and_5 (and_5_out, not_3_out, or_1_out);
  and and_6 (and_6_out, not_4_out, Cin);
  or or_2 (Co, and_4_out, and_3_out);
  or or_3 (S, and_5_out, and_6_out);

  // Notes on the sheet:
  //   A
  //   B
  //   Cin
  //   S
  //   Co
endmodule

module _4_b (
  input  in_1,
  input  in_2,
  input  in_3,
  input  in_4,
  input  in_5,
  input  B0,
  input  in_7,
  input  in_8,
  input  in_9,
  output out_10,
  output out_11,
  output out_12,
  output out_13,
  output out_14
);

  wire and_1_out, and_4_out, and_5_out, and_6_out, and_9_out, and_10_out, and_11_out, and_12_out, and_13_out,
       and_14_out, C0, C1, C2, G0, G1, G2, G3, P0, P1, P2, P3;

  and and_1 (and_1_out, P0, in_5);
  xor xor_1 (P0, in_1, B0);
  xor xor_2 (P1, in_2, in_7);
  and and_2 (G0, in_1, B0);
  and and_3 (G1, in_2, in_7);
  or or_1 (C0, and_1_out, G0);
  and and_4 (and_4_out, in_5, P2, P0, P1);
  and and_5 (and_5_out, P1, P2, G0);
  and and_6 (and_6_out, P2, G1);
  or or_2 (C2, and_4_out, G2, and_6_out, and_5_out);
  xor xor_3 (P2, in_3, in_8);
  xor xor_4 (P3, in_4, in_9);
  and and_7 (G2, in_3, in_8);
  and and_8 (G3, in_4, in_9);
  and and_9 (and_9_out, P0, P1, in_5);
  and and_10 (and_10_out, P1, G0);
  and and_11 (and_11_out, in_5, P0, P1, P2, P3);
  and and_12 (and_12_out, P3, P2, P1, G0);
  and and_13 (and_13_out, P3, P2, G1);
  and and_14 (and_14_out, P3, G2);
  or or_3 (C1, and_9_out, G1, and_10_out);
  or or_4 (out_14, G3, and_11_out, and_12_out, and_13_out, and_14_out);
  full__adder full_adder_1 (.A(in_1), .B(B0), .Cin(in_5), .S(out_10));  // open: Co
  full__adder full_adder_2 (.A(in_4), .B(in_9), .Cin(C2), .S(out_13));  // open: Co
  full__adder full_adder_3 (.A(in_2), .B(in_7), .Cin(C0), .S(out_11));  // open: Co
  full__adder full_adder_4 (.A(in_3), .B(in_8), .Cin(C1), .S(out_12));  // open: Co

  // Other names for the same wires on the sheet: A0 = in_1; A1 = in_2; A2 = in_3; A3 = in_4; B1 = in_7; B2 = in_8;
  //   B3 = in_9; Cin = in_5; Cout = out_14; S0 = out_10; S1 = out_11; S2 = out_12; S3 = out_13

  // Notes on the sheet:
  //   C0
  //   C2
  //   generating variables
  //   C1
  //   Cout
  //   FOR BIT 0
  //   FOR BIT 3
  //   Predicting Carries
  //   Implementation
  //   FOR BIT 1
  //   FOR BIT 2
endmodule

module alu_main (
  input  SUB,
  input  EN,
  input  [7:0] in_3,
  input  [7:0] in_4,
  input  in_5,
  input  in_6,
  input  in_7,
  output out_8,
  output out_9,
  output [7:0] Result,
  output [7:0] Result_2
);

  wire n4_b_1_out_14, xor_1_out, xor_2_out, xor_3_out, xor_4_out, xor_5_out, xor_6_out, xor_7_out, xor_8_out;
  wire [1:0] nor_1_out;

  xor xor_1 (xor_1_out, in_3[0], SUB);
  xor xor_2 (xor_2_out, in_3[1], SUB);
  xor xor_3 (xor_3_out, in_3[2], SUB);
  xor xor_4 (xor_4_out, in_3[3], SUB);
  xor xor_5 (xor_5_out, in_3[4], SUB);
  xor xor_6 (xor_6_out, in_3[5], SUB);
  xor xor_7 (xor_7_out, in_3[6], SUB);
  xor xor_8 (xor_8_out, in_3[7], SUB);
  _4_b u_4_b_1 (
    .in_1(in_4[0]), .in_2(in_4[1]), .in_3(in_4[2]), .in_4(in_4[3]), .B0(xor_1_out), .in_7(xor_2_out),
    .in_8(xor_3_out), .in_9(xor_4_out), .out_10(Result_2[0]), .out_11(Result_2[1]), .out_12(Result_2[2]),
    .out_13(Result_2[3]), .out_14(n4_b_1_out_14), .in_5(SUB));
  _4_b u_4_b_2 (
    .in_1(in_4[4]), .in_2(in_4[5]), .in_3(in_4[6]), .in_4(in_4[7]), .B0(xor_5_out), .in_7(xor_6_out),
    .in_8(xor_7_out), .in_9(xor_8_out), .out_10(Result_2[4]), .out_11(Result_2[5]), .out_12(Result_2[6]),
    .out_13(Result_2[7]), .out_14(nor_1_out[1]), .in_5(n4_b_1_out_14));
  assign Result[0] = EN ? Result_2[0] : 1'bz;  // Controlled_Buffer controlled_buffer_1
  assign Result[1] = EN ? Result_2[1] : 1'bz;  // Controlled_Buffer controlled_buffer_2
  assign Result[2] = EN ? Result_2[2] : 1'bz;  // Controlled_Buffer controlled_buffer_3
  assign Result[3] = EN ? Result_2[3] : 1'bz;  // Controlled_Buffer controlled_buffer_4
  assign Result[4] = EN ? Result_2[4] : 1'bz;  // Controlled_Buffer controlled_buffer_5
  assign Result[5] = EN ? Result_2[5] : 1'bz;  // Controlled_Buffer controlled_buffer_6
  assign Result[6] = EN ? Result_2[6] : 1'bz;  // Controlled_Buffer controlled_buffer_7
  assign Result[7] = EN ? Result_2[7] : 1'bz;  // Controlled_Buffer controlled_buffer_8
  nor nor_1 (nor_1_out[0], Result_2[0], Result_2[1], Result_2[2], Result_2[3], Result_2[3], Result_2[4], Result_2[5], Result_2[7]);
  Register #(.width(2)) register_1 (.D(nor_1_out), .en(in_5), .Q({out_8, out_9}), .clk(in_7), .clr(in_6));

  // Other names for the same wires on the sheet: ZF = out_9; CF = out_8; ENABLE = EN

  // Notes on the sheet:
  //   REGISTER B
  //   REGISTER A
  //   ALU
  //   RESULT
endmodule

module reg_built_in (
  input  Inpur_Enable,
  input  [3:0] in_2,
  input  in_3,
  input  in_4,
  input  in_5,
  output [3:0] out_6
);

  wire [3:0] controlled_buffer_1_out;

  assign controlled_buffer_1_out = Inpur_Enable ? in_2 : 4'bz;  // Controlled_Buffer controlled_buffer_1
  Register #(.width(4)) register_1 (.D(controlled_buffer_1_out), .en(in_3), .Q(out_6), .clk(in_5), .clr(in_4));
endmodule

module RAM_BUILT_IN (
  input  [7:0] in_1,
  input  [7:0] in_2,
  input  [3:0] M_In,
  input  SEL,
  input  in_5,
  input  in_6,
  input  in_7,
  input  in_8,
  input  in_9,
  input  in_10,
  input  in_11,
  input  in_12,
  output [3:0] out_13,
  output [7:0] out_14
);

  wire M_A_t, multiplexer_1_out;
  wire [3:0] reg_built_in_1_out_6;
  wire [7:0] I_p_RAM;

  Multiplexer #(.enable("false")) multiplexer_1 (.in0(in_9), .in1(in_12), .out(multiplexer_1_out), .sel(in_8));
  reg_built_in reg_built_in_1 (
    .in_2(in_1[3:0]), .in_3(1'b1), .in_4(in_5), .in_5(in_10), .out_6(reg_built_in_1_out_6),
    .Inpur_Enable(in_11));
  DotMatrix #(.matrixcols(4), .matrixrows(1), .dotshape("circle")) dotmatrix_1 (
    .col0(out_13[3]), .col1(out_13[2]), .col2(out_13[1]), .col3(out_13[0]));
  Multiplexer #(.width(4), .enable("false")) multiplexer_2 (
    .in0(reg_built_in_1_out_6), .in1(M_In), .out(out_13), .sel(M_A_t));
  DotMatrix #(.matrixcols(8), .matrixrows(1), .dotshape("circle")) dotmatrix_2 (
    .col0(out_14[7]), .col1(out_14[6]), .col2(out_14[5]), .col3(out_14[4]), .col4(out_14[3]),
    .col5(out_14[2]), .col6(out_14[1]), .col7(out_14[0]));
  RAM #(.addrWidth(4), .bus("separate")) ram_1 (
    .addr(out_13), .din(I_p_RAM), .data(out_14), .str(multiplexer_1_out), .sel(SEL), .clk(in_10), .ld(in_6),
    .clr(in_7));
  DotMatrix #(.matrixcols(8), .matrixrows(1), .dotshape("circle")) dotmatrix_3 (
    .col0(I_p_RAM[7]), .col1(I_p_RAM[6]), .col2(I_p_RAM[5]), .col3(I_p_RAM[4]), .col4(I_p_RAM[3]),
    .col5(I_p_RAM[2]), .col6(I_p_RAM[1]), .col7(I_p_RAM[0]));
  Multiplexer #(.width(8), .enable("false")) multiplexer_3 (.in0(in_1), .in1(in_2), .out(I_p_RAM), .sel(M_A_t));

  // Other names for the same wires on the sheet: B[7:0] = in_1; B1[3:0] = in_1[3:0]; B2[3:0] = in_1[7:4]; CLK = in_10;
  //   M_A = in_8; M_A_BITInput[7:0] = in_2; M_A_Input[3:0] = M_In; MI = in_11; RI = in_9; RO = in_6; RST = in_5
endmodule

module b2d (
  input  in_1,
  input  [7:0] in_2,
  input  in_3,
  input  in_4,
  output [7:0] out_5,
  output [7:0] out_6,
  output [7:0] out_7
);

  wire [7:0] n1bitregister_1_out_6;

  _1bitregister u_1bitregister_1 (
    .in_1(in_2), .EN(1'b1), .WR(in_1), .CLOCK(in_3), .CLR(in_4), .out_6(n1bitregister_1_out_6));
  ROM #(.dataWidth(24)) rom_1 (.addr(n1bitregister_1_out_6), .data({out_7, out_6, out_5}));  // open: sel

  // Notes on the sheet:
  //   contents of rom_1 (hex, n*v repeats v):
  //   0 1 2 3 4 5 6 7 8 9 100 101 102 103 104 105 106 107 108 109 200 201 202 203 204 205 206 207 208 209
  //   300 301 302 303 304 305 306 307 308 309 400 401 402 403 404 405 406 407 408 409 500 501 502 503 504
  //   505 506 507 508 509 600 601 602 603 604 605 606 607 608 609 700 701 702 703 704 705 706 707 708 709
  //   800 801 802 803 804 805 806 807 808 809 900 901 902 903 904 905 906 907 908 909 10000 10001 10002
  //   10003 10004 10005 10006 10007 10008 10009 10100 10101 10102 10103 10104 10105 10106 10107 10108
  //   10109 10200 10201 10202 10203 10204 10205 10206 10207 10208 10209 10300 10301 10302 10303 10304
  //   10305 10306 10307 10308 10309 10400 10401 10402 10403 10404 10405 10406 10407 10408 10409 10500
  //   10501 10502 10503 10504 10505 10506 10507 10508 10509 10600 10601 10602 10603 10604 10605 10606
  //   10607 10608 10609 10700 10701 10702 10703 10704 10705 10706 10707 10708 10709 10800 10801 10802
  //   10803 10804 10805 10806 10807 10808 10809 10900 10901 10902 10903 10904 10905 10906 10907 10908
  //   10909 20000 20001 20002 20003 20004 20005 20006 20007 20008 20009 20100 20101 20102 20103 20104
  //   20105 20106 20107 20108 20109 20200 20201 20202 20203 20204 20205 20206 20207 20208 20209 20300
  //   20301 20302 20303 20304 20305 20306 20307 20308 20309 20400 20401 20402 20403 20404 20405 20406
  //   20407 20408 20409 20500 20501 20502 20503 20504 20505
endmodule

module a1 (
  input  LOAD,
  input  I_P,
  input  CLK,
  input  CLR,
  output out_5
);

  wire and_1_out, and_2_out, not_1_out, or_1_out;

  Pull_Resistor #(.pull(1)) pull_resistor_1 (.node(I_P));
  and and_1 (and_1_out, out_5, not_1_out);
  not not_1 (not_1_out, LOAD);
  and and_2 (and_2_out, LOAD, I_P);
  or or_1 (or_1_out, and_1_out, and_2_out);
  reg_part reg_part_1 (.CLR(CLR), .I_P(or_1_out), .CLK(CLK), .out_4(out_5));  // open: out_5
endmodule

module _1bitregister (
  input  [7:0] in_1,
  input  EN,
  input  WR,
  input  CLOCK,
  input  CLR,
  output [7:0] out_6
);

  wire a1_1_out_5, a1_2_out_5, a1_3_out_5, a1_4_out_5, a1_5_out_5, a1_6_out_5, a1_7_out_5, a1_8_out_5;

  a1 a1_1 (.LOAD(WR), .I_P(in_1[7]), .CLK(CLOCK), .CLR(CLR), .out_5(a1_1_out_5));
  a1 a1_2 (.LOAD(WR), .I_P(in_1[6]), .CLK(CLOCK), .CLR(CLR), .out_5(a1_2_out_5));
  a1 a1_3 (.LOAD(WR), .I_P(in_1[5]), .CLK(CLOCK), .CLR(CLR), .out_5(a1_3_out_5));
  a1 a1_4 (.LOAD(WR), .I_P(in_1[4]), .CLK(CLOCK), .CLR(CLR), .out_5(a1_4_out_5));
  a1 a1_5 (.LOAD(WR), .I_P(in_1[3]), .CLK(CLOCK), .CLR(CLR), .out_5(a1_5_out_5));
  a1 a1_6 (.LOAD(WR), .I_P(in_1[2]), .CLK(CLOCK), .CLR(CLR), .out_5(a1_6_out_5));
  a1 a1_7 (.LOAD(WR), .I_P(in_1[1]), .CLK(CLOCK), .CLR(CLR), .out_5(a1_7_out_5));
  a1 a1_8 (.LOAD(WR), .I_P(in_1[0]), .CLK(CLOCK), .CLR(CLR), .out_5(a1_8_out_5));
  assign out_6[7] = EN ? a1_1_out_5 : 1'bz;  // Controlled_Buffer controlled_buffer_1
  assign out_6[6] = EN ? a1_2_out_5 : 1'bz;  // Controlled_Buffer controlled_buffer_2
  assign out_6[5] = EN ? a1_3_out_5 : 1'bz;  // Controlled_Buffer controlled_buffer_3
  assign out_6[4] = EN ? a1_4_out_5 : 1'bz;  // Controlled_Buffer controlled_buffer_4
  assign out_6[3] = EN ? a1_5_out_5 : 1'bz;  // Controlled_Buffer controlled_buffer_5
  assign out_6[2] = EN ? a1_6_out_5 : 1'bz;  // Controlled_Buffer controlled_buffer_6
  assign out_6[1] = EN ? a1_7_out_5 : 1'bz;  // Controlled_Buffer controlled_buffer_7
  assign out_6[0] = EN ? a1_8_out_5 : 1'bz;  // Controlled_Buffer controlled_buffer_8

  // Notes on the sheet:
  //   INPUT
  //   LOAD
endmodule

module reg_part (
  input  CLR,
  input  I_P,
  input  CLK,
  output out_4,
  output out_5
);

  wire and_1_out, and_2_out, and_3_out, not_1_out, not_2_out, not_3_out, not_4_out;

  not not_1 (not_1_out, not_2_out);
  not not_2 (not_2_out, CLK);
  not not_3 (not_3_out, I_P);
  and and_1 (and_1_out, CLK, not_4_out);
  not not_4 (not_4_out, not_1_out);
  and and_2 (and_2_out, not_3_out, and_1_out);
  and and_3 (and_3_out, and_1_out, I_P);
  nor nor_1 (out_4, and_2_out, CLR, out_5);
  nor nor_2 (out_5, out_4, and_3_out);
endmodule

module programcounter (
  input  Jump,
  input  [3:0] \input ,
  input  Count_Enable,
  input  Clock,
  input  Clear,
  output [3:0] Output
);

  Counter #(.width(4), .max('hf), .ongoal("stay")) counter_1 (
    .load(Jump), .D(\input ), .count(Count_Enable), .Q(Output), .clk(Clock), .clr(Clear));  // open: carry
endmodule

module reset (
  input  in_1,
  input  in_2,
  output out_3,
  output out_4,
  output out_5
);

  wire nand_1_out;

  not not_1 (out_3, in_1);
  not not_2 (out_4, out_3);
  nand nand_1 (nand_1_out, out_3, in_2);
  not not_3 (out_5, nand_1_out);
endmodule

module A_REG (
  input  in_1,
  input  in_2,
  input  [7:0] in_3,
  input  in_4,
  input  in_5,
  output [7:0] out_6
);

  _1bitregister u_1bitregister_1 (.in_1(in_3), .EN(in_2), .WR(in_1), .CLOCK(in_4), .CLR(in_5), .out_6(out_6));
endmodule

module B_REG (
  input  in_1,
  input  in_2,
  input  [7:0] in_3,
  input  in_4,
  input  in_5,
  output [7:0] out_6
);

  _1bitregister u_1bitregister_1 (.in_1(in_3), .EN(in_2), .WR(in_1), .CLOCK(in_4), .CLR(in_5), .out_6(out_6));
endmodule

// RST
module control_logic (
  input  in_1,
  input  STEP_RST,
  input  II,
  input  RST,
  input  [1:0] Carry,
  input  [3:0] INSTRUCTION,
  output out_7,
  output out_8,
  output out_9,
  output out_10,
  output out_11,
  output out_12,
  output out_13,
  output T5,
  output out_15,
  output out_16,
  output out_17,
  output out_18,
  output out_19,
  output out_20,
  output out_21,
  output out_22,
  output out_23
);

  wire decoder_1_out0, decoder_1_out1, decoder_1_out2, decoder_1_out3, decoder_1_out4, not_1_out;
  wire [2:0] counter_1_q;
  wire [3:0] reg_built_in_1_out_6;

  not not_1 (not_1_out, in_1);
  Counter #(.width(3), .max('h7)) counter_1 (
    .D(3'b000), .Q(counter_1_q), .clk(not_1_out), .clr(STEP_RST));  // open: load, count, carry
  reg_built_in reg_built_in_1 (
    .in_2(INSTRUCTION), .in_3(1'b1), .in_4(RST), .in_5(in_1), .out_6(reg_built_in_1_out_6), .Inpur_Enable(II));
  LED led_1 (.in(counter_1_q[0]));
  LED led_2 (.in(counter_1_q[1]));
  LED led_3 (.in(counter_1_q[2]));
  Decoder #(.select(3), .enable("false")) decoder_1 (
    .out0(decoder_1_out0), .out1(decoder_1_out1), .out2(decoder_1_out2), .out3(decoder_1_out3),
    .out4(decoder_1_out4), .out5(T5), .sel(counter_1_q));  // open: out6, out7
  DotMatrix #(.matrixcols(16), .matrixrows(1), .dotshape("circle")) dotmatrix_1 (
    .col0(out_23), .col1(out_22), .col2(out_21), .col3(out_20), .col4(out_19), .col5(out_18), .col6(out_17),
    .col7(out_16), .col8(out_15), .col9(out_13), .col10(out_12), .col11(out_11), .col12(out_10),
    .col13(out_9), .col14(out_8), .col15(out_7));
  LED led_4 (.in(decoder_1_out0));
  LED led_5 (.in(decoder_1_out1));
  LED led_6 (.in(decoder_1_out2));
  LED led_7 (.in(decoder_1_out3));
  LED led_8 (.in(decoder_1_out4));
  DotMatrix #(.matrixcols(9), .matrixrows(1), .dotshape("circle")) dotmatrix_2 (
    .col0(Carry[1]), .col1(Carry[0]), .col2(reg_built_in_1_out_6[3]), .col3(reg_built_in_1_out_6[2]),
    .col4(reg_built_in_1_out_6[1]), .col5(reg_built_in_1_out_6[0]), .col6(counter_1_q[2]),
    .col7(counter_1_q[1]), .col8(counter_1_q[0]));
  ROM #(.addrWidth(9), .dataWidth(16)) rom_1 (
    .addr({Carry, reg_built_in_1_out_6, counter_1_q}),
    .data({out_23, out_22, out_21, out_20, out_19, out_18, out_17, out_16, out_15, out_13, out_12, out_11, out_10, out_9, out_8, out_7}));  // open: sel

  // Other names for the same wires on the sheet: CLK = in_1

  // Notes on the sheet:
  //   contents of rom_1 (hex, n*v repeats v):
  //   2002 1028 6*0 2002 1028 12 48 4*0 2002 1028 12 408 8140 0 0 0 2002 1028 4010 5*0 2002 1028 12 84 4*0
  //   2002 1028 50 5*0 2002 1028 12 408 340 0 0 0 2002 1028 6*0 2002 1028 6*0 2002 1028 6*0 2002 1028 6*0
  //   2002 1028 6*0 2002 1028 6*0 2002 1028 6*0 2002 1028 880 5*0 2002 1028 1 5*0 2002 1028 6*0 2002 1028
  //   12 48 4*0 2002 1028 12 408 8140 0 0 0 2002 1028 4010 5*0 2002 1028 12 84 4*0 2002 1028 50 5*0 2002
  //   1028 12 408 340 0 0 0 2002 1028 6*0 2002 1028 6*0 2002 1028 6*0 2002 1028 4010 5*0 2002 1028 6*0
  //   2002 1028 6*0 2002 1028 6*0 2002 1028 880 5*0 2002 1028 1 5*0 2002 1028 6*0 2002 1028 12 48 4*0 2002
  //   1028 12 408 8140 0 0 0 2002 1028 4010 5*0 2002 1028 12 84 4*0 2002 1028 50 5*0 2002 1028 12 408 340
  //   0 0 0 2002 1028 6*0 2002 1028 6*0 2002 1028 4010 5*0 2002 1028 6*0 2002 1028 6*0 2002 1028 6*0 2002
  //   1028 6*0 2002 1028 880 5*0 2002 1028 1 5*0 2002 1028 6*0 2002 1028 12 48 4*0 2002 1028 12 408 8140 0
  //   0 0 2002 1028 4010 5*0 2002 1028 12 84 4*0 2002 1028 50 5*0 2002 1028 12 408 340 0 0 0 2002 1028 6*0
  //   2002 1028 4010 5*0 2002 1028 6*0 2002 1028 6*0 2002 1028 6*0 2002 1028 6*0 2002 1028 6*0 2002 1028
  //   880 5*0 2002 1028 1
endmodule

module IR (
  input  in_1,
  input  in_2,
  input  [7:0] in_3,
  input  in_4,
  input  in_5,
  output [7:0] out_6
);

  wire [7:4] n1bitregister_1_out_6;

  _1bitregister u_1bitregister_1 (
    .in_1(in_3), .EN(in_2), .WR(in_1), .CLOCK(in_4), .CLR(in_5), .out_6({n1bitregister_1_out_6, out_6[3:0]}));
  assign out_6[7:4] = in_2 ? 4'b0000 : 4'bz;  // Controlled_Buffer controlled_buffer_1
endmodule
