// Logisim project Register.circ as structural Verilog: 3 circuits, main circuit main
module main (
  input  in_1,
  input  in_2,
  output out_3,
  output out_4
);

  wire and_1_out, and_2_out, and_3_out, not_1_out, not_2_out, not_3_out, not_4_out;

  not not_1 (not_1_out, not_2_out);
  not not_2 (not_2_out, in_2);
  not not_3 (not_3_out, in_1);
  and and_1 (and_1_out, in_2, not_4_out);
  not not_4 (not_4_out, not_1_out);
  and and_2 (and_2_out, not_3_out, and_1_out);
  and and_3 (and_3_out, and_1_out, in_1);
  nor nor_1 (out_3, and_2_out, out_4);
  nor nor_2 (out_4, out_3, and_3_out);
endmodule

module a1 (
  input  in_1,
  input  in_2,
  input  in_3,
  output out_4
);

  wire and_1_out, and_2_out, not_1_out, or_1_out;

  and and_1 (and_1_out, out_4, not_1_out);
  not not_1 (not_1_out, in_1);
  and and_2 (and_2_out, in_1, in_2);
  main main_1 (.in_1(or_1_out), .in_2(in_3), .out_3(out_4));  // open: out_4
  or or_1 (or_1_out, and_1_out, and_2_out);
endmodule

module _1bitregister (
  input  in_1,
  input  INPUT,
  input  in_3,
  input  in_4,
  input  in_5,
  input  in_6,
  input  in_7,
  input  in_8,
  input  LOAD,
  output out_10,
  output out_11,
  output out_12,
  output out_13,
  output out_14,
  output out_15,
  output out_16,
  output out_17
);

  wire clock_1_out;

  Clock clock_1 (.out(clock_1_out));
  a1 a1_1 (.in_1(LOAD), .in_2(in_1), .in_3(clock_1_out), .out_4(out_10));
  a1 a1_2 (.in_1(LOAD), .in_2(INPUT), .in_3(clock_1_out), .out_4(out_11));
  a1 a1_3 (.in_1(LOAD), .in_2(in_3), .in_3(clock_1_out), .out_4(out_12));
  a1 a1_4 (.in_1(LOAD), .in_2(in_4), .in_3(clock_1_out), .out_4(out_13));
  a1 a1_5 (.in_1(LOAD), .in_2(in_5), .in_3(clock_1_out), .out_4(out_14));
  a1 a1_6 (.in_1(LOAD), .in_2(in_6), .in_3(clock_1_out), .out_4(out_15));
  a1 a1_7 (.in_1(LOAD), .in_2(in_7), .in_3(clock_1_out), .out_4(out_16));
  a1 a1_8 (.in_1(LOAD), .in_2(in_8), .in_3(clock_1_out), .out_4(out_17));

  // Notes on the sheet:
  //   CLOCK
endmodule
